// Logisim project Lab6.circ as structural Verilog
module P1_cronometro_sincrono (
  input  in_1,
  input  in_2,
  input  in_3
);

  wire clock_1_out;
  wire [6:0] p1_cronometro_sincrono_vhdl_1_qd_7s, p1_cronometro_sincrono_vhdl_1_qu_7s;

  Clock clock_1 (.out(clock_1_out));
  P1_cronometro_sincrono_vhdl p1_cronometro_sincrono_vhdl_1 (
    .clk(clock_1_out), .z(in_1), .ud(in_2), .sst(in_3), .qu_7s(p1_cronometro_sincrono_vhdl_1_qu_7s),
    .qd_7s(p1_cronometro_sincrono_vhdl_1_qd_7s));
  _7_Segment_Display u_7_segment_display_1 (
    .g(p1_cronometro_sincrono_vhdl_1_qd_7s[0]), .f(p1_cronometro_sincrono_vhdl_1_qd_7s[1]),
    .a(p1_cronometro_sincrono_vhdl_1_qd_7s[6]), .b(p1_cronometro_sincrono_vhdl_1_qd_7s[5]),
    .e(p1_cronometro_sincrono_vhdl_1_qd_7s[2]), .d(p1_cronometro_sincrono_vhdl_1_qd_7s[3]),
    .c(p1_cronometro_sincrono_vhdl_1_qd_7s[4]));  // open: dp
  _7_Segment_Display u_7_segment_display_2 (
    .g(p1_cronometro_sincrono_vhdl_1_qu_7s[0]), .f(p1_cronometro_sincrono_vhdl_1_qu_7s[1]),
    .a(p1_cronometro_sincrono_vhdl_1_qu_7s[6]), .b(p1_cronometro_sincrono_vhdl_1_qu_7s[5]),
    .e(p1_cronometro_sincrono_vhdl_1_qu_7s[2]), .d(p1_cronometro_sincrono_vhdl_1_qu_7s[3]),
    .c(p1_cronometro_sincrono_vhdl_1_qu_7s[4]));  // open: dp
endmodule

module P2_sequencia_qualquer (
  input  in_1
);

  wire clock_1_out;
  wire [6:0] p2_sequencia_qualquer_vhdl_1_lsd, p2_sequencia_qualquer_vhdl_1_msd;

  Clock clock_1 (.out(clock_1_out));
  P2_sequencia_qualquer_vhdl p2_sequencia_qualquer_vhdl_1 (
    .clk(clock_1_out), .start(in_1), .msd(p2_sequencia_qualquer_vhdl_1_msd),
    .lsd(p2_sequencia_qualquer_vhdl_1_lsd));
  _7_Segment_Display u_7_segment_display_1 (
    .g(p2_sequencia_qualquer_vhdl_1_lsd[0]), .f(p2_sequencia_qualquer_vhdl_1_lsd[1]),
    .a(p2_sequencia_qualquer_vhdl_1_lsd[6]), .b(p2_sequencia_qualquer_vhdl_1_lsd[5]),
    .e(p2_sequencia_qualquer_vhdl_1_lsd[2]), .d(p2_sequencia_qualquer_vhdl_1_lsd[3]),
    .c(p2_sequencia_qualquer_vhdl_1_lsd[4]));  // open: dp
  _7_Segment_Display u_7_segment_display_2 (
    .g(p2_sequencia_qualquer_vhdl_1_msd[0]), .f(p2_sequencia_qualquer_vhdl_1_msd[1]),
    .a(p2_sequencia_qualquer_vhdl_1_msd[6]), .b(p2_sequencia_qualquer_vhdl_1_msd[5]),
    .e(p2_sequencia_qualquer_vhdl_1_msd[2]), .d(p2_sequencia_qualquer_vhdl_1_msd[3]),
    .c(p2_sequencia_qualquer_vhdl_1_msd[4]));  // open: dp
endmodule

// VHDL entity P1_cronometro_sincrono_vhdl, as the project stores it:
library ieee;
use ieee.std_logic_1164.all;
use ieee.std_logic_unsigned.all;

entity P1_cronometro_sincrono_vhdl is
    port (
        clk      : in  std_logic; -- Período de 1s
        z        : in  std_logic; -- Reseta o contador e suspende a contagem 
        ud       : in  std_logic; -- low (0) -> ascendente, high (1) -> descendente.
        sst      : in  std_logic; -- Ativa / Para a Contagem
        qu_7s    : out std_logic_vector(6 downto 0);
        qd_7s    : out std_logic_vector(6 downto 0)
    );
end P1_cronometro_sincrono_vhdl;

architecture cronometro_sincrono_arch of P1_cronometro_sincrono_vhdl is
    signal u         : std_logic_vector(3 downto 0);
    signal d         : std_logic_vector(2 downto 0);
    signal dir_atual : std_logic; -- Registrador para armazenar a direção
begin
    proc: process(clk, z)
    begin
        -- Reset Assíncrono e Atualização de Direção
        if z = '1' then
            dir_atual <= ud; -- Atualiza a direção APENAS quando Z é acionado
            
            if ud = '0' then 
                -- Se for ascendente, reseta para 00
                u <= "0000";
                d <= "000";
            else             
                -- Se for descendente, reseta para 59
                u <= "1001";
                d <= "101";
            end if;
            
        -- Processamento Síncrono
        elsif rising_edge(clk) then
            if sst = '1' then -- Só conta se Start/Stop estiver ativo
                
                -- Usa o sinal 'dir_atual' travado, ignorando mudanças em 'ud' enquanto z='0'
                -- Ascendente
                if dir_atual = '0' then
                    if u < "1001" then
                        u <= u + "0001";
                    else
                        u <= "0000";
                        if d < "101" then
                            d <= d + "001";
                        else 
                            d <= "000";
                        end if;
                    end if;
                    
                -- Descendente    
                else 
                    if u > "0000" then
                        u <= u - "0001";
                    else
                        u <= "1001";
                        if d > "000" then
                            d <= d - "001";
                        else 
                            d <= "101";
                        end if;
                    end if;
                end if;
                
            end if;
        end if;
    end process proc;

    -- Display Unidades (Acionado pelo sinal 'u')
    with u select
        qu_7s <= "1111110" when "0000", -- 0
                 "0110000" when "0001", -- 1
                 "1101101" when "0010", -- 2
                 "1111001" when "0011", -- 3
                 "0110011" when "0100", -- 4
                 "1011011" when "0101", -- 5
                 "1011111" when "0110", -- 6
                 "1110000" when "0111", -- 7
                 "1111111" when "1000", -- 8
                 "1110011" when "1001", -- 9
                 "0000000" when others;

    -- Display Dezenas (Acionado pelo sinal 'd')
    with d select
        qd_7s <= "1111110" when "000", -- 0
                 "0110000" when "001", -- 1
                 "1101101" when "010", -- 2
                 "1111001" when "011", -- 3
                 "0110011" when "100", -- 4
                 "1011011" when "101", -- 5
                 "0000000" when others;

end cronometro_sincrono_arch;

// VHDL entity P2_sequencia_qualquer_vhdl, as the project stores it:
library ieee;
use ieee.std_logic_1164.all;
use ieee.std_logic_unsigned.all;

entity P2_sequencia_qualquer_vhdl is
	port (
		clk, start     :	in  std_logic;
		msd, lsd       :	out std_logic_vector(6 downto 0)                
    );
end P2_sequencia_qualquer_vhdl;

architecture sequencia_qualquer_arch of P2_sequencia_qualquer_vhdl is
	signal numero   :   std_logic_vector(6 downto 0);
	signal letra    :   std_logic_vector(6 downto 0) := "0000000";
	signal contador :   std_logic_vector(4 downto 0) := "00000";
begin
	ra: process(clk, start)
	begin
		if start = '1' then
			if clk = '1' and clk' event then
				if contador < "10001" then
					letra <= "1101111";
					case contador is
						when "00000" => numero <= "1101101"; letra <= "0000110"; -- 2  (I)
						when "00001" => numero <= "1110000"; letra <= "0000000"; -- 7
						when "00010" => numero <= "0110000"; letra <= "0000110"; -- 1  (I)
						when "00011" => numero <= "1110011"; letra <= "0000000"; -- 9
						when "00100" => numero <= "1111111"; letra <= "0000110"; -- 8  (I)
						when "00101" => numero <= "1011011"; letra <= "0000000"; -- 5
						when "00110" => numero <= "0110000"; letra <= "0000110"; -- 1  (I)
						when "00111" => numero <= "0000001"; letra <= "0000000"; -- -
						when "01000" => numero <= "0110000"; letra <= "0000110"; -- 1  (I)
						when "01001" => numero <= "1011011"; letra <= "0000000"; -- 5
						when "01010" => numero <= "1111111"; letra <= "0000110"; -- 8  (I)
						when "01011" => numero <= "1110011"; letra <= "0000000"; -- 9
						when "01100" => numero <= "0110000"; letra <= "0000110"; -- 1  (I)
						when "01101" => numero <= "1110000"; letra <= "0000000"; -- 7
						when "01110" => numero <= "1101101"; letra <= "0000110"; -- 2  (I)
						when "01111" => numero <= "0000001"; letra <= "0000000"; -- -
						when others  => numero <= "0000001"; letra <= "0000000"; -- traço
					end case;
					contador <= contador + "00001";
				end if;
			end if;
		else
			numero <="0000001";
			letra <="0000000";
			contador <= "00000";
		end if;
		msd(0) <= numero(0);
		msd(1) <= numero(1);
		msd(2) <= numero(2);
		msd(3) <= numero(3);
		msd(4) <= numero(4);
		msd(5) <= numero(5);
		msd(6) <= numero(6);
		lsd(0) <= letra(0);
		lsd(1) <= letra(1);
		lsd(2) <= letra(2);
		lsd(3) <= letra(3);
		lsd(4) <= letra(4);
		lsd(5) <= letra(5);
		lsd(6) <= letra(6);	
	end process ra;
end sequencia_qualquer_arch;
